# Fritzing sketch Big Button (saved by Fritzing 0.9.3b)
breadboards: 1

parts:
  S1 = Round Pushbutton
  S2 = Round Pushbutton
  S3 = Round Pushbutton
  S4 = Round Pushbutton
  S5 = Round Pushbutton
  R1 = Resistor [tolerance=±5% resistance=10k package=THT]
  R2 = Resistor [tolerance=±5% resistance=10k package=THT]
  R3 = Resistor [tolerance=±5% resistance=10k package=THT]
  R4 = Resistor [tolerance=±5% resistance=10k package=THT]
  R5 = Resistor [tolerance=±5% resistance=10k package=THT]
  Part1 = Arduino Nano (Rev3.0)

nets:
  N1: S1.leg0, Part1.D7
  N2: S2.leg0, Part1.D6
  N3: S3.leg0, Part1.D5
  N4: S4.leg0, Part1.D4
  N5: S5.leg0, Part1.D3
  N6: R1.Pin_0, R2.Pin_0, R3.Pin_0, R4.Pin_0, R5.Pin_0
